// Logisim project CPU.circ as structural Verilog
module main (
);

  ALU alu_1 ();  // open: CMD, A_IN, B_IN, OUT
  Register register_1 ();  // open: Clock, Adresse_1, Valeur_In, Valeur_2_out, Adresse_2, Valeur_3_out, Adresse_3
endmodule

module ALU (
  input  [2:0] CMD,
  input  [7:0] A_IN,
  input  [7:0] B_IN,
  output [7:0] OUT
);

  wire decoder_1_out0, decoder_1_out1, decoder_1_out2, decoder_1_out3, decoder_1_out4, decoder_1_out5,
       decoder_1_out6, decoder_1_out7;
  wire [7:0] adder_1_out, and_1_out, negator_1_out, not_1_out, or_1_out, shifter_1_out, shifter_2_out,
       subtractor_1_out;

  Decoder #(.select(3), .disabled(0), .enable("false")) decoder_1 (
    .out0(decoder_1_out0), .out1(decoder_1_out1), .out2(decoder_1_out2), .out3(decoder_1_out3),
    .out4(decoder_1_out4), .out5(decoder_1_out5), .out6(decoder_1_out6), .out7(decoder_1_out7), .sel(CMD));
  Transistor #(.\type ("n"), .width(8)) transistor_1 (.in(and_1_out), .out(OUT), .gate(decoder_1_out0));
  assign and_1_out = A_IN & B_IN;  // AND_Gate and_1, 8 bits wide
  assign or_1_out = A_IN | B_IN;  // OR_Gate or_1, 8 bits wide
  assign not_1_out = ~A_IN;  // NOT_Gate not_1, 8 bits wide
  Adder adder_1 (.a(A_IN), .b(B_IN), .out(adder_1_out));  // open: cin, cout
  Subtractor subtractor_1 (.a(A_IN), .b(B_IN), .out(subtractor_1_out));  // open: bin, bout
  Transistor #(.\type ("n"), .width(8)) transistor_2 (.in(or_1_out), .out(OUT), .gate(decoder_1_out1));
  Transistor #(.\type ("n"), .width(8)) transistor_3 (.in(not_1_out), .out(OUT), .gate(decoder_1_out2));
  Transistor #(.\type ("n"), .width(8)) transistor_4 (.in(adder_1_out), .out(OUT), .gate(decoder_1_out3));
  Shifter #(.shift("lr")) shifter_1 (.in(A_IN), .\dist (3'b001), .out(shifter_1_out));
  Shifter shifter_2 (.in(A_IN), .\dist (3'b001), .out(shifter_2_out));
  Negator negator_1 (.in(A_IN), .out(negator_1_out));
  Transistor #(.\type ("n"), .width(8)) transistor_5 (.in(subtractor_1_out), .out(OUT), .gate(decoder_1_out4));
  Transistor #(.\type ("n"), .width(8)) transistor_6 (.in(shifter_1_out), .out(OUT), .gate(decoder_1_out5));
  Transistor #(.\type ("n"), .width(8)) transistor_7 (.in(shifter_2_out), .out(OUT), .gate(decoder_1_out6));
  Transistor #(.\type ("n"), .width(8)) transistor_8 (.in(negator_1_out), .out(OUT), .gate(decoder_1_out7));
endmodule

module Register (
  input  Clock,
  input  [1:0] Adresse_1,
  input  [7:0] Valeur_In,
  input  [1:0] Adresse_2,
  input  [1:0] Adresse_3,
  output [7:0] Valeur_2_out,
  output [7:0] Valeur_3_out
);

  wire decoder_1_out0, decoder_1_out1, decoder_1_out2, decoder_1_out3;
  wire [7:0] A_q, B_q, C_q, D_q;

  Decoder #(.select(2), .enable("false")) decoder_1 (
    .out0(decoder_1_out0), .out1(decoder_1_out1), .out2(decoder_1_out2), .out3(decoder_1_out3),
    .sel(Adresse_1));
  Register_part A (.D(Valeur_In), .en(decoder_1_out0), .Q(A_q), .clk(Clock));  // open: clr
  Register_part B (.D(Valeur_In), .en(decoder_1_out1), .Q(B_q), .clk(Clock));  // open: clr
  Register_part C (.D(Valeur_In), .en(decoder_1_out2), .Q(C_q), .clk(Clock));  // open: clr
  Register_part D (.D(Valeur_In), .en(decoder_1_out3), .Q(D_q), .clk(Clock));  // open: clr
  Multiplexer #(.select(2), .width(8), .enable("false")) multiplexer_1 (
    .in0(A_q), .in1(B_q), .in2(C_q), .in3(D_q), .out(Valeur_2_out), .sel(Adresse_2));
  Multiplexer #(.select(2), .width(8), .enable("false")) multiplexer_2 (
    .in0(A_q), .in1(B_q), .in2(C_q), .in3(D_q), .out(Valeur_3_out), .sel(Adresse_3));
endmodule
